// Logisim project CPU.circ as structural Verilog
module Alu (
  input  [15:0] A,
  input  [15:0] B,
  input  [15:0] ALU_Output,
  input  [2:0] OpSelector,
  output Zero
);

  wire [15:0] adder_1_out, and_1_out, divider_1_out, multiplier_1_out, negator_1_out, nor_1_out, or_1_out,
       subtractor_1_out, undriven;

  Adder #(.width(16)) adder_1 (.a(A), .b(B), .out(adder_1_out));  // open: cin, cout
  Subtractor #(.width(16)) subtractor_1 (.a(A), .b(B), .out(subtractor_1_out));  // open: bin, bout
  Multiplier #(.width(16)) multiplier_1 (.a(A), .b(B), .out(multiplier_1_out));  // open: cin, cout
  Divider #(.width(16)) divider_1 (.a(A), .b(B), .out(divider_1_out));  // open: upper, rem
  Negator #(.width(16)) negator_1 (.in(B), .out(negator_1_out));
  assign and_1_out = A & B;  // AND_Gate and_1, 16 bits wide
  assign or_1_out = A | B;  // OR_Gate or_1, 16 bits wide
  assign nor_1_out = ~(A | B);  // NOR_Gate nor_1, 16 bits wide
  and and_2 (Zero, ~ALU_Output[0], ~ALU_Output[1], ~ALU_Output[2], ~ALU_Output[3], ~ALU_Output[4], ~ALU_Output[5], ~ALU_Output[6], ~ALU_Output[7], ~ALU_Output[8], ~ALU_Output[9], ~ALU_Output[10], ~ALU_Output[11], ~ALU_Output[12], ~ALU_Output[13], ~ALU_Output[14], ~ALU_Output[15]);  // AND_Gate
  Multiplexer #(.select(3), .width(16), .enable("false")) multiplexer_1 (
    .in0(undriven), .in1(adder_1_out), .in2(subtractor_1_out), .in3(multiplier_1_out), .in4(divider_1_out),
    .in5(negator_1_out), .in6(and_1_out), .in7(or_1_out), .out(ALU_Output), .sel(OpSelector));

  // Other names for the same wires on the sheet: X[15:0] = ALU_Output
endmodule

module Control_unit (
  input  [3:0] OpCode,
  input  [3:0] ALUop,
  output out_3,
  output out_4,
  output out_5,
  output out_6,
  output out_7,
  output out_8,
  output out_9
);

  and R_type (ALUop[2], ~OpCode[3], ~OpCode[2], ~OpCode[1], ~OpCode[0]);  // AND_Gate
  and lw (out_7, ~OpCode[3], ~OpCode[2], OpCode[1], OpCode[0]);  // AND_Gate
  and sw (out_9, OpCode[3], ~OpCode[2], OpCode[1], OpCode[0]);  // AND_Gate
  and beq (ALUop[0], OpCode[0], ~OpCode[1], ~OpCode[2], ~OpCode[3]);  // AND_Gate
  or or_1 (ALUop[1], out_9, out_7);
  or or_2 (out_5, out_7, out_9);
  or or_3 (out_6, ALUop[2], out_7);
  // Pins of 3 and 4 bits meet at ALUop

  assign out_3 = ALUop[0];
  assign out_4 = ALUop[2];
  assign out_8 = out_7;

  // Other names for the same wires on the sheet: X = ALUop[0]
endmodule

module Alu_control (
  input  [2:0] OpSelector,
  input  [3:0] \function ,
  input  [2:0] ALUop
);

  wire [2:0] multiplexer_2_out, multiplexer_3_out, multiplexer_4_out, undriven, undriven_2, undriven_3,
       undriven_4;

  Multiplexer #(.width(3), .enable("false")) multiplexer_1 (
    .in0(multiplexer_4_out), .in1(\function [3:1]), .out(OpSelector), .sel(ALUop[2]));
  Multiplexer #(.width(3), .enable("false")) multiplexer_2 (
    .in0(undriven), .in1(undriven_2), .out(multiplexer_2_out), .sel(ALUop[1]));
  Multiplexer #(.width(3), .enable("false")) multiplexer_3 (
    .in0(undriven_3), .in1(undriven_4), .out(multiplexer_3_out), .sel(ALUop[0]));
  Multiplexer #(.width(3), .enable("false")) multiplexer_4 (
    .in0(multiplexer_3_out), .in1(multiplexer_2_out), .out(multiplexer_4_out), .sel(ALUop[1]));

  // Notes on the sheet:
  //   0
  //   4
  //   0
  //   5
endmodule
